// Logisim project Project2ZacharyWillson.circ as structural Verilog: 4 circuits, main circuit main
module main (
);

  wire and_1_out, and_2_out, B0, B1, B2, B3, B4, B5, B6, B7, B8, B9, BL, BU, C0, C1, C2, CLK, L1_l, L1_u,
       not_1_out, or_8_out, P1_v, R0, R1, R3, R4, Valid;
  wire [2:0] counter_1_q;
  wire [3:0] IB1_c0, P1_b0, register_2_q, register_3_q, register_4_q, register_5_q;

  Button n1 (.out(B1));
  Button n4 (.out(B4));
  Button n7 (.out(B7));
  Button L (.out(BL));
  Button n3 (.out(B3));
  Button n2 (.out(B2));
  Button n6 (.out(B6));
  Button n5 (.out(B5));
  Button n9 (.out(B9));
  Button n8 (.out(B8));
  Button U (.out(BU));
  Button n0 (.out(B0));
  or or_1 (R0, B3, B2, B1);
  or or_2 (R1, B6, B5, B4);
  or or_3 (R3, B9, B8, B7);
  or or_4 (R4, BU, B0, BL);
  or or_5 (C0, B1, B4, B7, BL);
  or or_6 (C1, B2, B5, B8, B0);
  or or_7 (C2, B3, B6, B9, BU);
  Clock clock_1 (.out(CLK));
  nand nand_1 (Valid, IB1_c0[0], IB1_c0[1], IB1_c0[2], IB1_c0[3]);
  // Probe on P1_b0
  Panel P1 (
    .R0(R0), .R1(R1), .R2(R3), .R3(R4), .C0(C0), .C1(C1), .C2(C2), .B0(P1_b0[0]), .B1(P1_b0[1]),
    .B2(P1_b0[2]), .B3(P1_b0[3]), .V(P1_v));
  LED Press (.in(P1_v));
  // Probe on IB1_c0
  InputBuffer IB1 (
    .B0(P1_b0[0]), .B1(P1_b0[1]), .B2(P1_b0[2]), .B3(P1_b0[3]), .V(P1_v), .CLK(not_1_out), .C0(IB1_c0[0]),
    .C1(IB1_c0[1]), .C2(IB1_c0[2]), .C3(IB1_c0[3]));
  not not_1 (not_1_out, CLK);
  Register #(.width(4)) register_1 (.D(register_2_q), .en(Valid), .clk(CLK));  // open: Q, clr
  Lock L1 (.C0(IB1_c0[0]), .C1(IB1_c0[1]), .C2(IB1_c0[2]), .C3(IB1_c0[3]), .CLK(CLK), .L(L1_l), .U(L1_u));
  Counter #(.max('h7), .width(3)) counter_1 (
    .count(or_8_out), .Q(counter_1_q), .up(L1_u), .clk(CLK));  // open: load, D, carry, clr
  or or_8 (or_8_out, L1_l, L1_u);
  Register #(.width(4)) register_2 (.D(register_3_q), .en(Valid), .clk(CLK), .Q(register_2_q));  // open: clr
  LED Unlocked (.in(and_1_out));
  and and_1 (and_1_out, ~counter_1_q[0], ~counter_1_q[1], ~counter_1_q[2]);  // AND_Gate
  Register #(.width(4)) register_3 (.D(register_4_q), .en(Valid), .clk(CLK), .Q(register_3_q));  // open: clr
  LED Locked (.in(and_2_out));
  and and_2 (and_2_out, ~counter_1_q[0], ~counter_1_q[1], counter_1_q[2]);  // AND_Gate
  Register #(.width(4)) register_4 (.D(register_5_q), .en(Valid), .clk(CLK), .Q(register_4_q));  // open: clr
  Register #(.width(4)) register_5 (.D(IB1_c0), .en(Valid), .clk(CLK), .Q(register_5_q));  // open: clr
endmodule

module Panel (
  input  R0,
  input  R1,
  input  R2,
  input  R3,
  input  C0,
  input  C1,
  input  C2,
  output B0,
  output B1,
  output B2,
  output B3,
  output V
);
endmodule

module InputBuffer (
  input  B0,
  input  B1,
  input  B2,
  input  B3,
  input  V,
  input  CLK,
  output C0,
  output C1,
  output C2,
  output C3
);

  wire and_1_out, d_ff_1_q, V_Rising, xor_1_out;

  D_Flip_Flop d_ff_1 (.D(V), .clk(CLK), .Q(d_ff_1_q));  // open: Qn, preset, reset
  xor xor_1 (xor_1_out, V, d_ff_1_q);
  and and_1 (and_1_out, xor_1_out, V);
  D_Flip_Flop d_ff_2 (.D(and_1_out), .clk(CLK), .Q(V_Rising));  // open: Qn, preset, reset
  Multiplexer #(.width(4)) multiplexer_1 (
    .in0(4'b1111), .in1({B3, B2, B1, B0}), .out({C3, C2, C1, C0}), .sel(V_Rising));
endmodule

module Lock (
  input  C0,
  input  C1,
  input  C2,
  input  C3,
  input  CLK,
  output L,
  output U
);

  wire and_1_out, and_2_out, and_3_out, and_4_out, D_1_BUFFER_SET, D_2_BUFFER_SET, decoder_1_out0,
       decoder_1_out1, decoder_1_out2, decoder_1_out3, I_0, I_1, Locked, LOCKED_BASE, LOCKED_D_1, LOCKED_D_2,
       LOCKED_State_0, LOCKED_State_1, LOCKED_U_1, Locking, LOCKING_1, LOCKING_2, LOCKING_3, LOCKING_BASE,
       LOCKING_State_0, LOCKING_State_1, META_S0_a, Meta_State_0, Meta_State_1, not_1_out, NOT_I_0, NOT_I_1,
       or_3_out, or_4_out, or_5_out, Unlocked, UNLOCKED_BASE, UNLOCKED_D_1, UNLOCKED_D_2, UNLOCKED_L_1,
       UNLOCKED_S0_a, UNLOCKED_S0_b, UNLOCKED_State_0, UNLOCKED_State_1, Unlocking, UNLOCKING_1, UNLOCKING_2,
       UNLOCKING_3, UNLOCKING_BASE, UNLOCKING_State_0, UNLOCKING_State_1;

  not not_1 (not_1_out, C0);
  D_Flip_Flop d_ff_1 (.clk(CLK), .Q(LOCKING_State_1));  // open: D, Qn, preset, reset
  D_Flip_Flop d_ff_2 (.clk(CLK), .Q(LOCKED_State_1));  // open: D, Qn, preset, reset
  D_Flip_Flop d_ff_3 (.clk(CLK), .Q(UNLOCKING_State_1));  // open: D, Qn, preset, reset
  Demultiplexer #(.select(2)) demultiplexer_1 (
    .out0(Unlocked), .out1(Locking), .out2(Locked), .out3(Unlocking), .in(CLK),
    .sel({Meta_State_1, Meta_State_0}));
  and and_1 (and_1_out, C3, C2);
  and and_2 (and_2_out, C3, C1, C0);
  and and_3 (and_3_out, C3, C2);
  and and_4 (and_4_out, C3, C1, not_1_out);
  D_Flip_Flop #(.trigger("falling")) d_ff_4 (.clk(CLK), .Q(Meta_State_1));  // open: D, Qn, preset, reset
  or or_1 (I_1, and_1_out, and_2_out);
  or or_2 (I_0, and_3_out, and_4_out);
  Register #(.trigger("falling"), .width(4)) register_1 (
    .D({C3, C2, C1, C0}), .en(D_1_BUFFER_SET));  // open: clk, Q, clr
  and and_5 (D_1_BUFFER_SET, NOT_I_1, NOT_I_0, UNLOCKED_L_1);
  and and_6 (META_S0_a, UNLOCKED_L_1, NOT_I_1, I_0);
  and and_7 (UNLOCKED_S0_b, UNLOCKED_L_1, I_1, I_0);
  not not_2 (NOT_I_1, I_1);
  not not_3 (NOT_I_0, I_0);
  D_Flip_Flop #(.trigger("falling")) d_ff_5 (.D(or_3_out), .clk(CLK), .Q(UNLOCKED_State_1));  // open: Qn, preset, reset
  buf or_3 (or_3_out, D_1_BUFFER_SET);  // OR_Gate
  and and_8 (UNLOCKED_S0_a, NOT_I_1, I_0, UNLOCKED_BASE);
  D_Flip_Flop d_ff_6 (.clk(CLK), .Q(LOCKING_State_0));  // open: D, Qn, preset, reset
  D_Flip_Flop d_ff_7 (.clk(CLK), .Q(LOCKED_State_0));  // open: D, Qn, preset, reset
  D_Flip_Flop d_ff_8 (.clk(CLK), .Q(UNLOCKING_State_0));  // open: D, Qn, preset, reset
  Register #(.trigger("falling"), .width(4)) register_2 (
    .D({C3, C2, C1, C0}), .en(D_2_BUFFER_SET));  // open: clk, Q, clr
  Decoder #(.enable("false"), .select(2)) decoder_1 (
    .out0(decoder_1_out0), .out1(decoder_1_out1), .out2(decoder_1_out2), .out3(decoder_1_out3),
    .sel({I_1, I_0}));
  D_Flip_Flop #(.trigger("falling")) d_ff_9 (.D(or_4_out), .clk(CLK), .Q(Meta_State_0));  // open: Qn, preset, reset
  buf or_4 (or_4_out, META_S0_a);  // OR_Gate
  Demultiplexer #(.select(2)) demultiplexer_2 (
    .out0(UNLOCKED_BASE), .out1(UNLOCKED_L_1), .out2(UNLOCKED_D_1), .out3(UNLOCKED_D_2), .in(Unlocked),
    .sel({UNLOCKED_State_1, UNLOCKED_State_0}));
  Demultiplexer #(.select(2)) demultiplexer_3 (
    .out0(LOCKING_BASE), .out1(LOCKING_1), .out2(LOCKING_2), .out3(LOCKING_3), .in(Locking),
    .sel({LOCKING_State_1, LOCKING_State_0}));
  Demultiplexer #(.select(2)) demultiplexer_4 (
    .out0(LOCKED_BASE), .out1(LOCKED_U_1), .out2(LOCKED_D_1), .out3(LOCKED_D_2), .in(Locked),
    .sel({LOCKED_State_1, LOCKED_State_0}));
  Demultiplexer #(.select(2)) demultiplexer_5 (
    .out0(UNLOCKING_BASE), .out1(UNLOCKING_1), .out2(UNLOCKING_2), .out3(UNLOCKING_3), .in(Unlocking),
    .sel({UNLOCKING_State_1, UNLOCKING_State_0}));
  LED Digit (.in(decoder_1_out0));
  LED Lock (.in(decoder_1_out1));
  LED Unlock (.in(decoder_1_out2));
  LED Invalid (.in(decoder_1_out3));
  D_Flip_Flop #(.trigger("falling")) d_ff_10 (
    .D(or_5_out), .clk(CLK), .Q(UNLOCKED_State_0));  // open: Qn, preset, reset
  or or_5 (or_5_out, UNLOCKED_S0_a, UNLOCKED_S0_b);

  // Other names for the same wires on the sheet: UNLOCKED_S1_a = D_1_BUFFER_SET
endmodule
